// Logisim project 8bit_Computer_V2.circ as structural Verilog: 7 circuits, main circuit main
module main (
  input  in_1
);

  wire ALU_carry_flag, ALU_zero_flag, and_1_out, clock_1_out, multiplexer_2_out, multiplexer_11_out,
       not_1_out, not_2_out, or_1_out, register_1_q, register_2_q, RESET_out, START_out;
  wire [3:0] multiplexer_4_out, multiplexer_6_out, multiplexer_7_out;
  wire [7:0] ALU_alu_out, controlled_buffer_2_out, dipswitch_1_sw8, DUAL_REG_d1, DUAL_REG_d2, IO_REG_o0,
       IO_REG_o1, IO_REG_port_out, multiplexer_3_out, multiplexer_5_out, multiplexer_8_out,
       multiplexer_9_out, multiplexer_10_out, multiplexer_12_out, NUMBER_DISPLAY_dsp_out,
       NUMBER_DISPLAY_num_out, NUMBER_INPUT_num_out, pull_resistor_6_node, ram_1_dout;
  wire [7:2] undriven;
  wire [9:0] multiplexer_1_out, PROGRAM_COUNTER_addr1, PROGRAM_COUNTER_ctr_out, STACK_REG_addr_out;
  wire [16:0] PROGRAM_ROM_data;
  wire [23:0] INSTRC_ROM_data;

  Clock clock_1 (.out(clock_1_out));
  and and_1 (and_1_out, clock_1_out, ~INSTRC_ROM_data[23]);  // AND_Gate
  ROM #(.addrWidth(5), .dataWidth(24)) INSTRC_ROM (.addr(PROGRAM_ROM_data[16:12]), .data(INSTRC_ROM_data));
  SHIFT_REG STACK_REG (
    .SEN(INSTRC_ROM_data[9]), .POP_PUSH(INSTRC_ROM_data[10]), .ADDR_IN(PROGRAM_COUNTER_addr1),
    .CLK(and_1_out), .RST(or_1_out), .ADDR_OUT(STACK_REG_addr_out));
  Multiplexer #(.width(10)) multiplexer_1 (
    .in0(PROGRAM_ROM_data[9:0]), .in1(STACK_REG_addr_out), .out(multiplexer_1_out), .sel(INSTRC_ROM_data[8]));
  PROGRAM_CTR PROGRAM_COUNTER (
    .CTR_IN(multiplexer_1_out), .CTR_LOAD(multiplexer_2_out), .CLK(and_1_out), .CTR_RST(or_1_out),
    .ADDR1(PROGRAM_COUNTER_addr1), .CTR_OUT(PROGRAM_COUNTER_ctr_out));
  Multiplexer multiplexer_2 (
    .in0(INSTRC_ROM_data[12]), .in1(multiplexer_11_out), .out(multiplexer_2_out), .sel(INSTRC_ROM_data[10]));
  LED HLT (.in(INSTRC_ROM_data[23]));
  ROM #(.addrWidth(10), .dataWidth(17)) PROGRAM_ROM (.addr(PROGRAM_COUNTER_ctr_out), .data(PROGRAM_ROM_data));
  LED EO (.in(INSTRC_ROM_data[22]));
  LED SUB (.in(INSTRC_ROM_data[21]));
  LED BIT_AND (.in(INSTRC_ROM_data[20]));
  LED BIT_OR (.in(INSTRC_ROM_data[19]));
  LedBar #(.matrixcols(5)) ledbar_1 (
    .led0(PROGRAM_ROM_data[16]), .led1(PROGRAM_ROM_data[15]), .led2(PROGRAM_ROM_data[14]),
    .led3(PROGRAM_ROM_data[13]), .led4(PROGRAM_ROM_data[12]));
  LED BIT_XOR (.in(INSTRC_ROM_data[18]));
  Pull_Resistor pull_resistor_1 (.node(PROGRAM_ROM_data));
  LedBar #(.matrixcols(4)) ledbar_2 (
    .led0(PROGRAM_ROM_data[11]), .led1(PROGRAM_ROM_data[10]), .led2(PROGRAM_ROM_data[9]),
    .led3(PROGRAM_ROM_data[8]));
  LedBar #(.matrixcols(4)) ledbar_3 (
    .led0(PROGRAM_ROM_data[7]), .led1(PROGRAM_ROM_data[6]), .led2(PROGRAM_ROM_data[5]),
    .led3(PROGRAM_ROM_data[4]));
  LED BIT_RSH (.in(INSTRC_ROM_data[17]));
  LedBar #(.matrixcols(4)) ledbar_4 (
    .led0(PROGRAM_ROM_data[3]), .led1(PROGRAM_ROM_data[2]), .led2(PROGRAM_ROM_data[1]),
    .led3(PROGRAM_ROM_data[0]));
  Multiplexer #(.width(8)) multiplexer_3 (
    .in0(PROGRAM_ROM_data[7:0]), .in1(multiplexer_12_out), .out(multiplexer_3_out), .sel(INSTRC_ROM_data[2]));
  LED REN (.in(INSTRC_ROM_data[16]));
  Multiplexer #(.width(4)) multiplexer_4 (
    .in0(PROGRAM_ROM_data[11:8]), .in1(PROGRAM_ROM_data[7:4]), .out(multiplexer_4_out),
    .sel(INSTRC_ROM_data[5]));
  Multiplexer #(.width(8)) multiplexer_5 (
    .in0(multiplexer_3_out), .in1(controlled_buffer_2_out), .out(multiplexer_5_out), .sel(INSTRC_ROM_data[5]));
  LED DMX (.in(INSTRC_ROM_data[15]));
  Multiplexer #(.width(4)) multiplexer_6 (
    .in0(PROGRAM_ROM_data[3:0]), .in1(multiplexer_7_out), .out(multiplexer_6_out), .sel(INSTRC_ROM_data[14]));
  Multiplexer #(.width(4)) multiplexer_7 (
    .in0(multiplexer_4_out), .in1(PROGRAM_ROM_data[7:4]), .out(multiplexer_7_out), .sel(INSTRC_ROM_data[2]));
  Multiplexer #(.width(8)) multiplexer_8 (
    .in0(ALU_alu_out), .in1(multiplexer_5_out), .out(multiplexer_8_out), .sel(INSTRC_ROM_data[15]));
  LED WMX (.in(INSTRC_ROM_data[14]));
  REG_8bit_4 DUAL_REG (
    .REG_EN(INSTRC_ROM_data[16]), .DATA(multiplexer_8_out), .CLK(and_1_out), .REG_RST(or_1_out),
    .REG_ADDR1(PROGRAM_ROM_data[11:8]), .REG_ADDR2(PROGRAM_ROM_data[7:4]), .WE_ADDR(multiplexer_6_out),
    .D1(DUAL_REG_d1), .D2(DUAL_REG_d2));
  LED AMX (.in(INSTRC_ROM_data[13]));
  Pull_Resistor pull_resistor_2 (.node(DUAL_REG_d2));
  or or_1 (or_1_out, START_out, RESET_out);
  Button RESET (.out(RESET_out));
  LED CLD (.in(INSTRC_ROM_data[12]));
  LED FLI (.in(INSTRC_ROM_data[11]));
  Multiplexer #(.width(8)) multiplexer_9 (
    .in0(PROGRAM_ROM_data[7:0]), .in1({4'b0000, PROGRAM_ROM_data[3:0]}), .out(multiplexer_9_out),
    .sel(INSTRC_ROM_data[5]));
  Pull_Resistor pull_resistor_3 (.node(DUAL_REG_d1));
  Multiplexer #(.width(8)) multiplexer_10 (
    .in0(DUAL_REG_d2), .in1(multiplexer_9_out), .out(multiplexer_10_out), .sel(INSTRC_ROM_data[13]));
  LED PP_PS (.in(INSTRC_ROM_data[10]));
  Register #(.width(1)) register_1 (
    .D(ALU_zero_flag), .en(INSTRC_ROM_data[11]), .clk(and_1_out), .Q(register_1_q), .clr(or_1_out));
  ALU_8bit ALU (
    .ALU_SUB(INSTRC_ROM_data[21]), .ALU_AND(INSTRC_ROM_data[20]), .ALU_OR(INSTRC_ROM_data[19]),
    .ALU_XOR(INSTRC_ROM_data[18]), .ALU_RSH(INSTRC_ROM_data[17]), .EO(INSTRC_ROM_data[22]), .D1(DUAL_REG_d1),
    .D2(multiplexer_10_out), .Carry_flag(ALU_carry_flag), .ALU_OUT(ALU_alu_out), .Zero_flag(ALU_zero_flag));
  LED SEN (.in(INSTRC_ROM_data[9]));
  Multiplexer #(.select(2)) multiplexer_11 (
    .in0(register_1_q), .in1(not_1_out), .in2(register_2_q), .in3(not_2_out), .out(multiplexer_11_out),
    .sel(PROGRAM_ROM_data[11:10]));
  not not_1 (not_1_out, register_1_q);
  Register #(.width(1)) register_2 (
    .D(ALU_carry_flag), .en(INSTRC_ROM_data[11]), .clk(and_1_out), .Q(register_2_q), .clr(or_1_out));
  LED SMX (.in(INSTRC_ROM_data[8]));
  not not_2 (not_2_out, register_2_q);
  LED MW (.in(INSTRC_ROM_data[7]));
  Pull_Resistor pull_resistor_4 (.node(ALU_alu_out[7:4]));
  RAM #(.enables("line")) ram_1 (
    .addr(ALU_alu_out), .we(INSTRC_ROM_data[7]), .clk(and_1_out), .din(pull_resistor_6_node),
    .dout(ram_1_dout));
  Pull_Resistor pull_resistor_5 (.node(ALU_alu_out));
  Pull_Resistor pull_resistor_6 (.node(pull_resistor_6_node));
  assign pull_resistor_6_node = INSTRC_ROM_data[6] ? DUAL_REG_d2 : 8'bz;  // Controlled_Buffer controlled_buffer_1
  assign controlled_buffer_2_out = INSTRC_ROM_data[6] ? ram_1_dout : 8'bz;  // Controlled_Buffer controlled_buffer_2
  LED MEN (.in(INSTRC_ROM_data[6]));
  Multiplexer #(.width(8)) multiplexer_12 (
    .in0(IO_REG_port_out), .in1(DUAL_REG_d2), .out(multiplexer_12_out), .sel(INSTRC_ROM_data[4]));
  Pull_Resistor pull_resistor_7 (.node(ram_1_dout));
  LED MMX (.in(INSTRC_ROM_data[5]));
  LED PW (.in(INSTRC_ROM_data[4]));
  LED PEN (.in(INSTRC_ROM_data[3]));
  IO IO_REG (
    .PORT_ADDR(ALU_alu_out[3:0]), .PORT_EN(INSTRC_ROM_data[3]), .I0(NUMBER_DISPLAY_num_out),
    .I1(NUMBER_DISPLAY_dsp_out), .I2(NUMBER_INPUT_num_out), .WEN(INSTRC_ROM_data[4]), .CLK(and_1_out),
    .RST(or_1_out), .PORT_IN(DUAL_REG_d2), .O0(IO_REG_o0), .O1(IO_REG_o1), .PORT_OUT(IO_REG_port_out));  // open: I3, I4, I5, I6, I7, I8, I9, I10, I11, I12, I13, I14, I15, O2, O3, O4, O5, O6, O7, O8, O9, O10, O11, O12, O13, O14, O15
  LED PMX (.in(INSTRC_ROM_data[2]));
  NUM_DSP NUMBER_DISPLAY (
    .DSP_SIGN(IO_REG_o1), .NUM_IN(IO_REG_o0), .NUM_OUT(NUMBER_DISPLAY_num_out),
    .DSP_OUT(NUMBER_DISPLAY_dsp_out));
  NUM_DSP NUMBER_INPUT (
    .DSP_SIGN({undriven, in_1, 1'b1}), .NUM_IN(dipswitch_1_sw8), .NUM_OUT(NUMBER_INPUT_num_out));  // open: DSP_OUT
  Button START (.out(START_out));
  DipSwitch dipswitch_1 (
    .sw1(dipswitch_1_sw8[7]), .sw2(dipswitch_1_sw8[6]), .sw3(dipswitch_1_sw8[5]), .sw4(dipswitch_1_sw8[4]),
    .sw5(dipswitch_1_sw8[3]), .sw6(dipswitch_1_sw8[2]), .sw7(dipswitch_1_sw8[1]), .sw8(dipswitch_1_sw8[0]));

  // Notes on the sheet:
  //   contents of INSTRC_ROM (hex, n*v repeats v):
  //   0 800000 410800 610800 510800 490800 450800 430800 1c000 416800 1000 400 1600 1300 41e060 41a0e0
  //   41e00c 41a01c
  //   contents of PROGRAM_ROM (hex, n*v repeats v):
  //   8301 11031 10012 9101 2234 11020 2032 2043 91ff b00b a004 1000
endmodule

module ALU_8bit (
  input  [7:0] D1,
  input  [7:0] D2,
  input  EO,
  input  ALU_SUB,
  input  ALU_AND,
  input  ALU_OR,
  input  ALU_XOR,
  input  ALU_RSH,
  output Zero_flag,
  output Carry_flag,
  output [7:0] ALU_OUT
);

  wire and_2_out, and_3_out, and_4_out, and_5_out, and_6_out;
  wire [7:0] adder_1_out, and_1_out, controlled_buffer_1_out, controlled_buffer_2_out,
       controlled_buffer_3_out, controlled_buffer_4_out, controlled_buffer_5_out, or_1_out, or_2_out,
       shifter_1_out, xor_1_out, xor_9_out;

  xor xor_1 (xor_1_out[0], D2[0], ALU_SUB);
  xor xor_2 (xor_1_out[1], D2[1], ALU_SUB);
  xor xor_3 (xor_1_out[2], D2[2], ALU_SUB);
  xor xor_4 (xor_1_out[3], D2[3], ALU_SUB);
  xor xor_5 (xor_1_out[4], D2[4], ALU_SUB);
  xor xor_6 (xor_1_out[5], D2[5], ALU_SUB);
  xor xor_7 (xor_1_out[6], D2[6], ALU_SUB);
  xor xor_8 (xor_1_out[7], D2[7], ALU_SUB);
  assign and_1_out = D1 & D2;  // AND_Gate and_1, 8 bits wide
  assign or_1_out = D1 | D2;  // OR_Gate or_1, 8 bits wide
  assign xor_9_out = D1 ^ D2;  // XOR_Gate xor_9, 8 bits wide
  Shifter #(.shift("lr")) shifter_1 (.in(D1), .\dist (3'b001), .out(shifter_1_out));
  LED ZFLAG_LED (.in(Zero_flag));
  Adder adder_1 (.a(D1), .b(xor_1_out), .out(adder_1_out), .cin(ALU_SUB), .cout(Carry_flag));
  nor nor_1 (Zero_flag, adder_1_out[7], adder_1_out[6], adder_1_out[5], adder_1_out[4], adder_1_out[3], adder_1_out[2], adder_1_out[1], adder_1_out[0]);
  LED CFLAG_LED (.in(Carry_flag));
  assign controlled_buffer_1_out = and_2_out ? adder_1_out : 8'bz;  // Controlled_Buffer controlled_buffer_1
  and and_2 (and_2_out, ~ALU_AND, ~ALU_OR, ~ALU_XOR, ~ALU_RSH);  // AND_Gate
  LED SUB_LED (.in(ALU_SUB));
  assign controlled_buffer_2_out = and_3_out ? and_1_out : 8'bz;  // Controlled_Buffer controlled_buffer_2
  assign controlled_buffer_3_out = and_4_out ? or_1_out : 8'bz;  // Controlled_Buffer controlled_buffer_3
  assign controlled_buffer_4_out = and_5_out ? xor_9_out : 8'bz;  // Controlled_Buffer controlled_buffer_4
  and and_3 (and_3_out, ~ALU_SUB, ALU_AND, ~ALU_OR, ~ALU_XOR, ~ALU_RSH);  // AND_Gate
  assign controlled_buffer_5_out = and_6_out ? shifter_1_out : 8'bz;  // Controlled_Buffer controlled_buffer_5
  and and_4 (and_4_out, ~ALU_SUB, ~ALU_AND, ALU_OR, ~ALU_XOR, ~ALU_RSH);  // AND_Gate
  LED AND_LED (.in(ALU_AND));
  and and_5 (and_5_out, ~ALU_SUB, ~ALU_AND, ~ALU_OR, ALU_XOR, ~ALU_RSH);  // AND_Gate
  LED OR_LED (.in(ALU_OR));
  Pull_Resistor pull_resistor_1 (.node(controlled_buffer_1_out));
  and and_6 (and_6_out, ~ALU_SUB, ~ALU_AND, ~ALU_OR, ~ALU_XOR, ALU_RSH);  // AND_Gate
  LED XOR_LED (.in(ALU_XOR));
  Pull_Resistor pull_resistor_2 (.node(controlled_buffer_2_out));
  Pull_Resistor pull_resistor_3 (.node(controlled_buffer_3_out));
  Pull_Resistor pull_resistor_4 (.node(controlled_buffer_4_out));
  Pull_Resistor pull_resistor_5 (.node(controlled_buffer_5_out));
  LED RSH_LED (.in(ALU_RSH));
  assign or_2_out = controlled_buffer_1_out | controlled_buffer_2_out | controlled_buffer_3_out | controlled_buffer_4_out | controlled_buffer_5_out;  // OR_Gate or_2, 8 bits wide
  assign ALU_OUT = EO ? or_2_out : 8'bz;  // Controlled_Buffer controlled_buffer_6
  LED EO_LED (.in(EO));
endmodule

module REG_8bit_4 (
  input  [7:0] DATA,
  input  [3:0] REG_ADDR1,
  input  [3:0] REG_ADDR2,
  input  [3:0] WE_ADDR,
  input  REG_EN,
  input  CLK,
  input  REG_RST,
  output [7:0] D1,
  output [7:0] D2
);

  wire decoder_1_out0, decoder_1_out1, decoder_1_out2, decoder_1_out3, decoder_1_out4, decoder_1_out5,
       decoder_1_out6, decoder_1_out7, decoder_1_out8, decoder_1_out9, decoder_1_out10, decoder_1_out11,
       decoder_1_out12, decoder_1_out13, decoder_1_out14, decoder_1_out15, decoder_2_out0, decoder_2_out1,
       decoder_2_out2, decoder_2_out3, decoder_2_out4, decoder_2_out5, decoder_2_out6, decoder_2_out7,
       decoder_2_out8, decoder_2_out9, decoder_2_out10, decoder_2_out11, decoder_2_out12, decoder_2_out13,
       decoder_2_out14, decoder_2_out15, decoder_3_out0, decoder_3_out1, decoder_3_out2, decoder_3_out3,
       decoder_3_out4, decoder_3_out5, decoder_3_out6, decoder_3_out7, decoder_3_out8, decoder_3_out9,
       decoder_3_out10, decoder_3_out11, decoder_3_out12, decoder_3_out13, decoder_3_out14, decoder_3_out15,
       or_1_out, or_2_out, or_3_out, or_4_out, or_5_out, or_6_out, or_7_out, or_8_out, or_9_out, or_10_out,
       or_11_out, or_12_out, or_13_out, or_14_out, or_15_out, or_16_out, pull_resistor_1_node,
       pull_resistor_2_node, pull_resistor_3_node, pull_resistor_4_node, pull_resistor_5_node,
       pull_resistor_6_node, pull_resistor_7_node, pull_resistor_8_node, pull_resistor_9_node,
       pull_resistor_10_node, pull_resistor_11_node, pull_resistor_12_node, pull_resistor_13_node,
       pull_resistor_14_node, pull_resistor_15_node, pull_resistor_16_node;
  wire [7:0] controlled_buffer_17_out, controlled_buffer_18_out, controlled_buffer_19_out,
       controlled_buffer_20_out, controlled_buffer_21_out, controlled_buffer_22_out,
       controlled_buffer_23_out, controlled_buffer_24_out, controlled_buffer_25_out,
       controlled_buffer_26_out, controlled_buffer_27_out, controlled_buffer_28_out,
       controlled_buffer_29_out, controlled_buffer_30_out, controlled_buffer_31_out,
       controlled_buffer_32_out, multiplexer_1_out, multiplexer_2_out, register_1_q, register_2_q,
       register_3_q, register_4_q, register_5_q, register_6_q, register_7_q, register_8_q, register_9_q,
       register_10_q, register_11_q, register_12_q, register_13_q, register_14_q, register_15_q,
       register_16_q;

  // LedBar #(.inputtype("row"), .matrixcols(4)) REG_ADDR1_LED: pin names not known; wires that end beside it: REG_ADDR1
  // LedBar #(.inputtype("row"), .matrixcols(4)) REG_ADDR2_LED: pin names not known; wires that end beside it: REG_ADDR2
  // LedBar #(.inputtype("row"), .matrixcols(4)) WE_ADDR_LED: pin names not known; wires that end beside it: WE_ADDR
  Decoder #(.select(4)) decoder_1 (
    .out0(decoder_1_out0), .out1(decoder_1_out1), .out2(decoder_1_out2), .out3(decoder_1_out3),
    .out4(decoder_1_out4), .out5(decoder_1_out5), .out6(decoder_1_out6), .out7(decoder_1_out7),
    .out8(decoder_1_out8), .out9(decoder_1_out9), .out10(decoder_1_out10), .out11(decoder_1_out11),
    .out12(decoder_1_out12), .out13(decoder_1_out13), .out14(decoder_1_out14), .out15(decoder_1_out15),
    .sel(REG_ADDR2));  // open: en
  Decoder #(.select(4)) decoder_2 (
    .out0(decoder_2_out0), .out1(decoder_2_out1), .out2(decoder_2_out2), .out3(decoder_2_out3),
    .out4(decoder_2_out4), .out5(decoder_2_out5), .out6(decoder_2_out6), .out7(decoder_2_out7),
    .out8(decoder_2_out8), .out9(decoder_2_out9), .out10(decoder_2_out10), .out11(decoder_2_out11),
    .out12(decoder_2_out12), .out13(decoder_2_out13), .out14(decoder_2_out14), .out15(decoder_2_out15),
    .sel(REG_ADDR1));  // open: en
  Decoder #(.select(4)) decoder_3 (
    .out0(decoder_3_out0), .out1(decoder_3_out1), .out2(decoder_3_out2), .out3(decoder_3_out3),
    .out4(decoder_3_out4), .out5(decoder_3_out5), .out6(decoder_3_out6), .out7(decoder_3_out7),
    .out8(decoder_3_out8), .out9(decoder_3_out9), .out10(decoder_3_out10), .out11(decoder_3_out11),
    .out12(decoder_3_out12), .out13(decoder_3_out13), .out14(decoder_3_out14), .out15(decoder_3_out15),
    .sel(WE_ADDR));  // open: en
  or or_1 (or_1_out, decoder_2_out0, decoder_1_out0);
  or or_2 (or_2_out, decoder_2_out1, decoder_1_out1);
  or or_3 (or_3_out, decoder_2_out2, decoder_1_out2);
  or or_4 (or_4_out, decoder_2_out3, decoder_1_out3);
  or or_5 (or_5_out, decoder_2_out4, decoder_1_out4);
  or or_6 (or_6_out, decoder_2_out5, decoder_1_out5);
  or or_7 (or_7_out, decoder_2_out6, decoder_1_out6);
  or or_8 (or_8_out, decoder_2_out7, decoder_1_out7);
  or or_9 (or_9_out, decoder_2_out8, decoder_1_out8);
  or or_10 (or_10_out, decoder_2_out9, decoder_1_out9);
  or or_11 (or_11_out, decoder_2_out10, decoder_1_out10);
  or or_12 (or_12_out, decoder_2_out11, decoder_1_out11);
  or or_13 (or_13_out, decoder_2_out12, decoder_1_out12);
  or or_14 (or_14_out, decoder_2_out13, decoder_1_out13);
  or or_15 (or_15_out, decoder_2_out14, decoder_1_out14);
  or or_16 (or_16_out, decoder_2_out15, decoder_1_out15);
  LED REG_EN_LED (.in(REG_EN));
  Pull_Resistor pull_resistor_1 (.node(pull_resistor_1_node));
  assign pull_resistor_1_node = REG_EN ? decoder_3_out0 : 1'bz;  // Controlled_Buffer controlled_buffer_1
  Pull_Resistor pull_resistor_2 (.node(pull_resistor_2_node));
  assign pull_resistor_2_node = REG_EN ? decoder_3_out1 : 1'bz;  // Controlled_Buffer controlled_buffer_2
  Pull_Resistor pull_resistor_3 (.node(pull_resistor_3_node));
  assign pull_resistor_3_node = REG_EN ? decoder_3_out2 : 1'bz;  // Controlled_Buffer controlled_buffer_3
  Pull_Resistor pull_resistor_4 (.node(pull_resistor_4_node));
  assign pull_resistor_4_node = REG_EN ? decoder_3_out3 : 1'bz;  // Controlled_Buffer controlled_buffer_4
  Pull_Resistor pull_resistor_5 (.node(pull_resistor_5_node));
  assign pull_resistor_5_node = REG_EN ? decoder_3_out4 : 1'bz;  // Controlled_Buffer controlled_buffer_5
  Pull_Resistor pull_resistor_6 (.node(pull_resistor_6_node));
  assign pull_resistor_6_node = REG_EN ? decoder_3_out5 : 1'bz;  // Controlled_Buffer controlled_buffer_6
  Pull_Resistor pull_resistor_7 (.node(pull_resistor_7_node));
  assign pull_resistor_7_node = REG_EN ? decoder_3_out6 : 1'bz;  // Controlled_Buffer controlled_buffer_7
  Pull_Resistor pull_resistor_8 (.node(pull_resistor_8_node));
  assign pull_resistor_8_node = REG_EN ? decoder_3_out7 : 1'bz;  // Controlled_Buffer controlled_buffer_8
  Pull_Resistor pull_resistor_9 (.node(pull_resistor_9_node));
  assign pull_resistor_9_node = REG_EN ? decoder_3_out8 : 1'bz;  // Controlled_Buffer controlled_buffer_9
  Pull_Resistor pull_resistor_10 (.node(pull_resistor_10_node));
  assign pull_resistor_10_node = REG_EN ? decoder_3_out9 : 1'bz;  // Controlled_Buffer controlled_buffer_10
  Pull_Resistor pull_resistor_11 (.node(pull_resistor_11_node));
  assign pull_resistor_11_node = REG_EN ? decoder_3_out10 : 1'bz;  // Controlled_Buffer controlled_buffer_11
  Pull_Resistor pull_resistor_12 (.node(pull_resistor_12_node));
  assign pull_resistor_12_node = REG_EN ? decoder_3_out11 : 1'bz;  // Controlled_Buffer controlled_buffer_12
  Pull_Resistor pull_resistor_13 (.node(pull_resistor_13_node));
  assign pull_resistor_13_node = REG_EN ? decoder_3_out12 : 1'bz;  // Controlled_Buffer controlled_buffer_13
  Pull_Resistor pull_resistor_14 (.node(pull_resistor_14_node));
  assign pull_resistor_14_node = REG_EN ? decoder_3_out13 : 1'bz;  // Controlled_Buffer controlled_buffer_14
  Pull_Resistor pull_resistor_15 (.node(pull_resistor_15_node));
  assign pull_resistor_15_node = REG_EN ? decoder_3_out14 : 1'bz;  // Controlled_Buffer controlled_buffer_15
  Pull_Resistor pull_resistor_16 (.node(pull_resistor_16_node));
  assign pull_resistor_16_node = REG_EN ? decoder_3_out15 : 1'bz;  // Controlled_Buffer controlled_buffer_16
  LED CLK_LED (.in(CLK));
  // LedBar #(.inputtype("row")) DATA_IN_LED: pin names not known; wires that end beside it: DATA
  Register register_1 (.D({8{1'b0}}), .en(pull_resistor_1_node), .clk(CLK), .Q(register_1_q), .clr(REG_RST));
  Register register_2 (.D(DATA), .en(pull_resistor_2_node), .clk(CLK), .Q(register_2_q), .clr(REG_RST));
  Register register_3 (.D(DATA), .en(pull_resistor_3_node), .clk(CLK), .Q(register_3_q), .clr(REG_RST));
  Register register_4 (.D(DATA), .en(pull_resistor_4_node), .clk(CLK), .Q(register_4_q), .clr(REG_RST));
  Register register_5 (.D(DATA), .en(pull_resistor_5_node), .clk(CLK), .Q(register_5_q), .clr(REG_RST));
  Register register_6 (.D(DATA), .en(pull_resistor_6_node), .clk(CLK), .Q(register_6_q), .clr(REG_RST));
  Register register_7 (.D(DATA), .en(pull_resistor_7_node), .clk(CLK), .Q(register_7_q), .clr(REG_RST));
  Register register_8 (.D(DATA), .en(pull_resistor_8_node), .clk(CLK), .Q(register_8_q), .clr(REG_RST));
  Register register_9 (.D(DATA), .en(pull_resistor_9_node), .clk(CLK), .Q(register_9_q), .clr(REG_RST));
  Register register_10 (.D(DATA), .en(pull_resistor_10_node), .clk(CLK), .Q(register_10_q), .clr(REG_RST));
  Register register_11 (.D(DATA), .en(pull_resistor_11_node), .clk(CLK), .Q(register_11_q), .clr(REG_RST));
  Register register_12 (.D(DATA), .en(pull_resistor_12_node), .clk(CLK), .Q(register_12_q), .clr(REG_RST));
  Register register_13 (.D(DATA), .en(pull_resistor_13_node), .clk(CLK), .Q(register_13_q), .clr(REG_RST));
  Register register_14 (.D(DATA), .en(pull_resistor_14_node), .clk(CLK), .Q(register_14_q), .clr(REG_RST));
  Register register_15 (.D(DATA), .en(pull_resistor_15_node), .clk(CLK), .Q(register_15_q), .clr(REG_RST));
  Register register_16 (.D(DATA), .en(pull_resistor_16_node), .clk(CLK), .Q(register_16_q), .clr(REG_RST));
  assign controlled_buffer_17_out = or_1_out ? register_1_q : 8'bz;  // Controlled_Buffer controlled_buffer_17
  assign controlled_buffer_18_out = or_2_out ? register_2_q : 8'bz;  // Controlled_Buffer controlled_buffer_18
  assign controlled_buffer_19_out = or_3_out ? register_3_q : 8'bz;  // Controlled_Buffer controlled_buffer_19
  assign controlled_buffer_20_out = or_4_out ? register_4_q : 8'bz;  // Controlled_Buffer controlled_buffer_20
  assign controlled_buffer_21_out = or_5_out ? register_5_q : 8'bz;  // Controlled_Buffer controlled_buffer_21
  assign controlled_buffer_22_out = or_6_out ? register_6_q : 8'bz;  // Controlled_Buffer controlled_buffer_22
  assign controlled_buffer_23_out = or_7_out ? register_7_q : 8'bz;  // Controlled_Buffer controlled_buffer_23
  assign controlled_buffer_24_out = or_8_out ? register_8_q : 8'bz;  // Controlled_Buffer controlled_buffer_24
  assign controlled_buffer_25_out = or_9_out ? register_9_q : 8'bz;  // Controlled_Buffer controlled_buffer_25
  assign controlled_buffer_26_out = or_10_out ? register_10_q : 8'bz;  // Controlled_Buffer controlled_buffer_26
  assign controlled_buffer_27_out = or_11_out ? register_11_q : 8'bz;  // Controlled_Buffer controlled_buffer_27
  assign controlled_buffer_28_out = or_12_out ? register_12_q : 8'bz;  // Controlled_Buffer controlled_buffer_28
  assign controlled_buffer_29_out = or_13_out ? register_13_q : 8'bz;  // Controlled_Buffer controlled_buffer_29
  assign controlled_buffer_30_out = or_14_out ? register_14_q : 8'bz;  // Controlled_Buffer controlled_buffer_30
  assign controlled_buffer_31_out = or_15_out ? register_15_q : 8'bz;  // Controlled_Buffer controlled_buffer_31
  assign controlled_buffer_32_out = or_16_out ? register_16_q : 8'bz;  // Controlled_Buffer controlled_buffer_32
  Multiplexer #(.select(4), .width(8)) multiplexer_1 (
    .in0(controlled_buffer_17_out), .in1(controlled_buffer_18_out), .in2(controlled_buffer_19_out),
    .in3(controlled_buffer_20_out), .in4(controlled_buffer_21_out), .in5(controlled_buffer_22_out),
    .in6(controlled_buffer_23_out), .in7(controlled_buffer_24_out), .in8(controlled_buffer_25_out),
    .in9(controlled_buffer_26_out), .in10(controlled_buffer_27_out), .in11(controlled_buffer_28_out),
    .in12(controlled_buffer_29_out), .in13(controlled_buffer_30_out), .in14(controlled_buffer_31_out),
    .in15(controlled_buffer_32_out), .out(multiplexer_1_out), .sel(REG_ADDR1));
  Multiplexer #(.select(4), .width(8)) multiplexer_2 (
    .in0(controlled_buffer_17_out), .in1(controlled_buffer_18_out), .in2(controlled_buffer_19_out),
    .in3(controlled_buffer_20_out), .in4(controlled_buffer_21_out), .in5(controlled_buffer_22_out),
    .in6(controlled_buffer_23_out), .in7(controlled_buffer_24_out), .in8(controlled_buffer_25_out),
    .in9(controlled_buffer_26_out), .in10(controlled_buffer_27_out), .in11(controlled_buffer_28_out),
    .in12(controlled_buffer_29_out), .in13(controlled_buffer_30_out), .in14(controlled_buffer_31_out),
    .in15(controlled_buffer_32_out), .out(multiplexer_2_out), .sel(REG_ADDR2));
  assign D1 = REG_EN ? multiplexer_1_out : 8'bz;  // Controlled_Buffer controlled_buffer_33
  assign D2 = REG_EN ? multiplexer_2_out : 8'bz;  // Controlled_Buffer controlled_buffer_34
endmodule

module PROGRAM_CTR (
  input  [9:0] CTR_IN,
  input  CTR_LOAD,
  input  CLK,
  input  CTR_RST,
  output [9:0] ADDR1,
  output [9:0] CTR_OUT
);

  wire [9:0] multiplexer_1_out;

  LED CTR_LOAD_LED (.in(CTR_LOAD));
  Multiplexer #(.width(10)) multiplexer_1 (.in0(ADDR1), .in1(CTR_IN), .out(multiplexer_1_out), .sel(CTR_LOAD));
  LED CLK_LED (.in(CLK));
  Register #(.width(10)) register_1 (.D(multiplexer_1_out), .en(1'b1), .clk(CLK), .Q(CTR_OUT), .clr(CTR_RST));
  LED CTR_RST_LED (.in(CTR_RST));
  Adder #(.width(10)) adder_1 (.a(CTR_OUT), .b({10{1'b0}}), .out(ADDR1), .cin(1'b1));  // open: cout
endmodule

module SHIFT_REG (
  input  [9:0] ADDR_IN,
  input  SEN,
  input  POP_PUSH,
  input  CLK,
  input  RST,
  output [9:0] ADDR_OUT
);

  wire not_1_out, pull_resistor_2_node;
  wire [9:0] controlled_buffer_4_out, controlled_buffer_6_out, controlled_buffer_7_out,
       controlled_buffer_9_out, controlled_buffer_10_out, controlled_buffer_12_out, controlled_buffer_13_out,
       controlled_buffer_15_out, controlled_buffer_16_out, controlled_buffer_18_out,
       controlled_buffer_19_out, controlled_buffer_21_out, controlled_buffer_22_out,
       controlled_buffer_24_out, controlled_buffer_25_out, controlled_buffer_27_out,
       controlled_buffer_28_out, controlled_buffer_30_out, controlled_buffer_31_out,
       controlled_buffer_33_out, controlled_buffer_34_out, controlled_buffer_36_out,
       controlled_buffer_37_out, controlled_buffer_39_out, controlled_buffer_40_out,
       controlled_buffer_42_out, controlled_buffer_43_out, controlled_buffer_45_out,
       controlled_buffer_46_out, controlled_buffer_48_out, controlled_buffer_49_out, pull_resistor_1_node,
       register_1_q, register_2_q, register_3_q, register_4_q, register_5_q, register_6_q, register_7_q,
       register_8_q, register_9_q, register_10_q, register_11_q, register_12_q, register_13_q, register_14_q,
       register_15_q, register_16_q, register_17_q;

  LED SEN_LED (.in(SEN));
  LED PPPS_LED (.in(POP_PUSH));
  Register #(.width(10)) register_1 (
    .D(pull_resistor_1_node), .en(pull_resistor_2_node), .clk(pull_resistor_2_node), .Q(register_1_q),
    .clr(RST));
  Pull_Resistor pull_resistor_1 (.node(pull_resistor_1_node));
  not not_1 (not_1_out, POP_PUSH);
  Pull_Resistor pull_resistor_2 (.node(pull_resistor_2_node));
  assign pull_resistor_2_node = SEN ? CLK : 1'bz;  // Controlled_Buffer controlled_buffer_1
  LED CLK_LED (.in(CLK));
  assign pull_resistor_1_node = not_1_out ? register_2_q : 10'bz;  // Controlled_Buffer controlled_buffer_2
  LED RST_LED (.in(RST));
  assign ADDR_OUT = SEN ? register_1_q : 10'bz;  // Controlled_Buffer controlled_buffer_3
  Register #(.width(10)) register_2 (
    .D(controlled_buffer_4_out), .en(pull_resistor_2_node), .clk(pull_resistor_2_node), .Q(register_2_q),
    .clr(RST));
  assign controlled_buffer_4_out = POP_PUSH ? ADDR_IN : 10'bz;  // Controlled_Buffer controlled_buffer_4
  assign controlled_buffer_4_out = not_1_out ? register_3_q : 10'bz;  // Controlled_Buffer controlled_buffer_5
  Register #(.width(10)) register_3 (
    .D(controlled_buffer_7_out), .en(pull_resistor_2_node), .clk(pull_resistor_2_node), .Q(register_3_q),
    .clr(RST));
  assign controlled_buffer_6_out = POP_PUSH ? register_2_q : 10'bz;  // Controlled_Buffer controlled_buffer_6
  assign controlled_buffer_7_out = POP_PUSH ? controlled_buffer_6_out : 10'bz;  // Controlled_Buffer controlled_buffer_7
  assign controlled_buffer_7_out = not_1_out ? register_4_q : 10'bz;  // Controlled_Buffer controlled_buffer_8
  assign controlled_buffer_9_out = POP_PUSH ? register_3_q : 10'bz;  // Controlled_Buffer controlled_buffer_9
  Register #(.width(10)) register_4 (
    .D(controlled_buffer_10_out), .en(pull_resistor_2_node), .clk(pull_resistor_2_node), .Q(register_4_q),
    .clr(RST));
  assign controlled_buffer_10_out = POP_PUSH ? controlled_buffer_9_out : 10'bz;  // Controlled_Buffer controlled_buffer_10
  assign controlled_buffer_10_out = not_1_out ? register_5_q : 10'bz;  // Controlled_Buffer controlled_buffer_11
  Register #(.width(10)) register_5 (
    .D(controlled_buffer_13_out), .en(pull_resistor_2_node), .clk(pull_resistor_2_node), .Q(register_5_q),
    .clr(RST));
  assign controlled_buffer_12_out = POP_PUSH ? register_4_q : 10'bz;  // Controlled_Buffer controlled_buffer_12
  assign controlled_buffer_13_out = POP_PUSH ? controlled_buffer_12_out : 10'bz;  // Controlled_Buffer controlled_buffer_13
  assign controlled_buffer_13_out = not_1_out ? register_6_q : 10'bz;  // Controlled_Buffer controlled_buffer_14
  assign controlled_buffer_15_out = POP_PUSH ? register_5_q : 10'bz;  // Controlled_Buffer controlled_buffer_15
  Register #(.width(10)) register_6 (
    .D(controlled_buffer_16_out), .en(pull_resistor_2_node), .clk(pull_resistor_2_node), .Q(register_6_q),
    .clr(RST));
  assign controlled_buffer_16_out = POP_PUSH ? controlled_buffer_15_out : 10'bz;  // Controlled_Buffer controlled_buffer_16
  assign controlled_buffer_16_out = not_1_out ? register_7_q : 10'bz;  // Controlled_Buffer controlled_buffer_17
  Register #(.width(10)) register_7 (
    .D(controlled_buffer_19_out), .en(pull_resistor_2_node), .clk(pull_resistor_2_node), .Q(register_7_q),
    .clr(RST));
  assign controlled_buffer_18_out = POP_PUSH ? register_6_q : 10'bz;  // Controlled_Buffer controlled_buffer_18
  assign controlled_buffer_19_out = POP_PUSH ? controlled_buffer_18_out : 10'bz;  // Controlled_Buffer controlled_buffer_19
  assign controlled_buffer_19_out = not_1_out ? register_8_q : 10'bz;  // Controlled_Buffer controlled_buffer_20
  assign controlled_buffer_21_out = POP_PUSH ? register_7_q : 10'bz;  // Controlled_Buffer controlled_buffer_21
  Register #(.width(10)) register_8 (
    .D(controlled_buffer_22_out), .en(pull_resistor_2_node), .clk(pull_resistor_2_node), .Q(register_8_q),
    .clr(RST));
  assign controlled_buffer_22_out = POP_PUSH ? controlled_buffer_21_out : 10'bz;  // Controlled_Buffer controlled_buffer_22
  assign controlled_buffer_22_out = not_1_out ? register_9_q : 10'bz;  // Controlled_Buffer controlled_buffer_23
  Register #(.width(10)) register_9 (
    .D(controlled_buffer_25_out), .en(pull_resistor_2_node), .clk(pull_resistor_2_node), .Q(register_9_q),
    .clr(RST));
  assign controlled_buffer_24_out = POP_PUSH ? register_8_q : 10'bz;  // Controlled_Buffer controlled_buffer_24
  assign controlled_buffer_25_out = POP_PUSH ? controlled_buffer_24_out : 10'bz;  // Controlled_Buffer controlled_buffer_25
  assign controlled_buffer_25_out = not_1_out ? register_10_q : 10'bz;  // Controlled_Buffer controlled_buffer_26
  assign controlled_buffer_27_out = POP_PUSH ? register_9_q : 10'bz;  // Controlled_Buffer controlled_buffer_27
  Register #(.width(10)) register_10 (
    .D(controlled_buffer_28_out), .en(pull_resistor_2_node), .clk(pull_resistor_2_node), .Q(register_10_q),
    .clr(RST));
  assign controlled_buffer_28_out = POP_PUSH ? controlled_buffer_27_out : 10'bz;  // Controlled_Buffer controlled_buffer_28
  assign controlled_buffer_28_out = not_1_out ? register_11_q : 10'bz;  // Controlled_Buffer controlled_buffer_29
  Register #(.width(10)) register_11 (
    .D(controlled_buffer_31_out), .en(pull_resistor_2_node), .clk(pull_resistor_2_node), .Q(register_11_q),
    .clr(RST));
  assign controlled_buffer_30_out = POP_PUSH ? register_10_q : 10'bz;  // Controlled_Buffer controlled_buffer_30
  assign controlled_buffer_31_out = POP_PUSH ? controlled_buffer_30_out : 10'bz;  // Controlled_Buffer controlled_buffer_31
  assign controlled_buffer_31_out = not_1_out ? register_12_q : 10'bz;  // Controlled_Buffer controlled_buffer_32
  assign controlled_buffer_33_out = POP_PUSH ? register_11_q : 10'bz;  // Controlled_Buffer controlled_buffer_33
  Register #(.width(10)) register_12 (
    .D(controlled_buffer_34_out), .en(pull_resistor_2_node), .clk(pull_resistor_2_node), .Q(register_12_q),
    .clr(RST));
  assign controlled_buffer_34_out = POP_PUSH ? controlled_buffer_33_out : 10'bz;  // Controlled_Buffer controlled_buffer_34
  assign controlled_buffer_34_out = not_1_out ? register_13_q : 10'bz;  // Controlled_Buffer controlled_buffer_35
  Register #(.width(10)) register_13 (
    .D(controlled_buffer_37_out), .en(pull_resistor_2_node), .clk(pull_resistor_2_node), .Q(register_13_q),
    .clr(RST));
  assign controlled_buffer_36_out = POP_PUSH ? register_12_q : 10'bz;  // Controlled_Buffer controlled_buffer_36
  assign controlled_buffer_37_out = POP_PUSH ? controlled_buffer_36_out : 10'bz;  // Controlled_Buffer controlled_buffer_37
  assign controlled_buffer_37_out = not_1_out ? register_14_q : 10'bz;  // Controlled_Buffer controlled_buffer_38
  assign controlled_buffer_39_out = POP_PUSH ? register_13_q : 10'bz;  // Controlled_Buffer controlled_buffer_39
  Register #(.width(10)) register_14 (
    .D(controlled_buffer_40_out), .en(pull_resistor_2_node), .clk(pull_resistor_2_node), .Q(register_14_q),
    .clr(RST));
  assign controlled_buffer_40_out = POP_PUSH ? controlled_buffer_39_out : 10'bz;  // Controlled_Buffer controlled_buffer_40
  assign controlled_buffer_40_out = not_1_out ? register_15_q : 10'bz;  // Controlled_Buffer controlled_buffer_41
  Register #(.width(10)) register_15 (
    .D(controlled_buffer_43_out), .en(pull_resistor_2_node), .clk(pull_resistor_2_node), .Q(register_15_q),
    .clr(RST));
  assign controlled_buffer_42_out = POP_PUSH ? register_14_q : 10'bz;  // Controlled_Buffer controlled_buffer_42
  assign controlled_buffer_43_out = POP_PUSH ? controlled_buffer_42_out : 10'bz;  // Controlled_Buffer controlled_buffer_43
  assign controlled_buffer_43_out = not_1_out ? register_16_q : 10'bz;  // Controlled_Buffer controlled_buffer_44
  assign controlled_buffer_45_out = POP_PUSH ? register_15_q : 10'bz;  // Controlled_Buffer controlled_buffer_45
  Register #(.width(10)) register_16 (
    .D(controlled_buffer_46_out), .en(pull_resistor_2_node), .clk(pull_resistor_2_node), .Q(register_16_q),
    .clr(RST));
  assign controlled_buffer_46_out = POP_PUSH ? controlled_buffer_45_out : 10'bz;  // Controlled_Buffer controlled_buffer_46
  assign controlled_buffer_46_out = not_1_out ? register_17_q : 10'bz;  // Controlled_Buffer controlled_buffer_47
  Register #(.width(10)) register_17 (
    .D(controlled_buffer_49_out), .en(pull_resistor_2_node), .clk(pull_resistor_2_node), .Q(register_17_q),
    .clr(RST));
  assign controlled_buffer_48_out = POP_PUSH ? register_16_q : 10'bz;  // Controlled_Buffer controlled_buffer_48
  assign controlled_buffer_49_out = POP_PUSH ? controlled_buffer_48_out : 10'bz;  // Controlled_Buffer controlled_buffer_49
  Pull_Resistor pull_resistor_3 (.node(register_17_q));
endmodule

module IO (
  input  [7:0] I0,
  input  [7:0] I1,
  input  [7:0] I2,
  input  [7:0] I3,
  input  [7:0] I4,
  input  [7:0] I5,
  input  [7:0] I6,
  input  [7:0] I7,
  input  [7:0] I8,
  input  [7:0] I9,
  input  [7:0] I10,
  input  [7:0] I11,
  input  [7:0] I12,
  input  [7:0] I13,
  input  [7:0] I14,
  input  [7:0] I15,
  input  [7:0] PORT_IN,
  input  [3:0] PORT_ADDR,
  input  PORT_EN,
  input  WEN,
  input  CLK,
  input  RST,
  output [7:0] PORT_OUT,
  output [7:0] O0,
  output [7:0] O1,
  output [7:0] O2,
  output [7:0] O3,
  output [7:0] O4,
  output [7:0] O5,
  output [7:0] O6,
  output [7:0] O7,
  output [7:0] O8,
  output [7:0] O9,
  output [7:0] O10,
  output [7:0] O11,
  output [7:0] O12,
  output [7:0] O13,
  output [7:0] O14,
  output [7:0] O15
);

  wire decoder_1_out0, decoder_1_out1, decoder_1_out2, decoder_1_out3, decoder_1_out4, decoder_1_out5,
       decoder_1_out6, decoder_1_out7, decoder_1_out8, decoder_1_out9, decoder_1_out10, decoder_1_out11,
       decoder_1_out12, decoder_1_out13, decoder_1_out14, decoder_1_out15, multiplexer_2_out,
       multiplexer_4_out, multiplexer_6_out, multiplexer_8_out, multiplexer_10_out, multiplexer_12_out,
       multiplexer_14_out, multiplexer_16_out, multiplexer_18_out, multiplexer_20_out, multiplexer_22_out,
       multiplexer_24_out, multiplexer_26_out, multiplexer_28_out, multiplexer_30_out, multiplexer_32_out;
  wire [7:0] multiplexer_1_out, multiplexer_3_out, multiplexer_5_out, multiplexer_7_out, multiplexer_9_out,
       multiplexer_11_out, multiplexer_13_out, multiplexer_15_out, multiplexer_17_out, multiplexer_19_out,
       multiplexer_21_out, multiplexer_23_out, multiplexer_25_out, multiplexer_27_out, multiplexer_29_out,
       multiplexer_31_out, multiplexer_33_out;

  LED PORT_EN_LED (.in(PORT_EN));
  Decoder #(.select(4)) decoder_1 (
    .out0(decoder_1_out0), .out1(decoder_1_out1), .out2(decoder_1_out2), .out3(decoder_1_out3),
    .out4(decoder_1_out4), .out5(decoder_1_out5), .out6(decoder_1_out6), .out7(decoder_1_out7),
    .out8(decoder_1_out8), .out9(decoder_1_out9), .out10(decoder_1_out10), .out11(decoder_1_out11),
    .out12(decoder_1_out12), .out13(decoder_1_out13), .out14(decoder_1_out14), .out15(decoder_1_out15),
    .sel(PORT_ADDR), .en(PORT_EN));
  LED PORT_WEN (.in(WEN));
  LED CLK_LED (.in(CLK));
  LED RST_LED (.in(RST));
  Multiplexer #(.width(8)) multiplexer_1 (.in0(I0), .in1(PORT_IN), .out(multiplexer_1_out), .sel(WEN));
  Multiplexer multiplexer_2 (.in0(1'b1), .in1(decoder_1_out0), .out(multiplexer_2_out), .sel(WEN));
  Multiplexer #(.width(8)) multiplexer_3 (.in0(I1), .in1(PORT_IN), .out(multiplexer_3_out), .sel(WEN));
  Multiplexer multiplexer_4 (.in0(1'b1), .in1(decoder_1_out1), .out(multiplexer_4_out), .sel(WEN));
  Multiplexer #(.width(8)) multiplexer_5 (.in0(I2), .in1(PORT_IN), .out(multiplexer_5_out), .sel(WEN));
  Multiplexer multiplexer_6 (.in0(1'b1), .in1(decoder_1_out2), .out(multiplexer_6_out), .sel(WEN));
  Multiplexer #(.width(8)) multiplexer_7 (.in0(I3), .in1(PORT_IN), .out(multiplexer_7_out), .sel(WEN));
  Multiplexer multiplexer_8 (.in0(1'b1), .in1(decoder_1_out3), .out(multiplexer_8_out), .sel(WEN));
  Multiplexer #(.width(8)) multiplexer_9 (.in0(I4), .in1(PORT_IN), .out(multiplexer_9_out), .sel(WEN));
  Multiplexer multiplexer_10 (.in0(1'b1), .in1(decoder_1_out4), .out(multiplexer_10_out), .sel(WEN));
  Multiplexer #(.width(8)) multiplexer_11 (.in0(I5), .in1(PORT_IN), .out(multiplexer_11_out), .sel(WEN));
  Multiplexer multiplexer_12 (.in0(1'b1), .in1(decoder_1_out5), .out(multiplexer_12_out), .sel(WEN));
  Multiplexer #(.width(8)) multiplexer_13 (.in0(I6), .in1(PORT_IN), .out(multiplexer_13_out), .sel(WEN));
  Multiplexer multiplexer_14 (.in0(1'b1), .in1(decoder_1_out6), .out(multiplexer_14_out), .sel(WEN));
  Multiplexer #(.width(8)) multiplexer_15 (.in0(I7), .in1(PORT_IN), .out(multiplexer_15_out), .sel(WEN));
  Multiplexer multiplexer_16 (.in0(1'b1), .in1(decoder_1_out7), .out(multiplexer_16_out), .sel(WEN));
  Multiplexer #(.width(8)) multiplexer_17 (.in0(I8), .in1(PORT_IN), .out(multiplexer_17_out), .sel(WEN));
  Multiplexer multiplexer_18 (.in0(1'b1), .in1(decoder_1_out8), .out(multiplexer_18_out), .sel(WEN));
  Multiplexer #(.width(8)) multiplexer_19 (.in0(I9), .in1(PORT_IN), .out(multiplexer_19_out), .sel(WEN));
  Multiplexer multiplexer_20 (.in0(1'b1), .in1(decoder_1_out9), .out(multiplexer_20_out), .sel(WEN));
  Multiplexer #(.width(8)) multiplexer_21 (.in0(I10), .in1(PORT_IN), .out(multiplexer_21_out), .sel(WEN));
  Multiplexer multiplexer_22 (.in0(1'b1), .in1(decoder_1_out10), .out(multiplexer_22_out), .sel(WEN));
  Multiplexer #(.width(8)) multiplexer_23 (.in0(I11), .in1(PORT_IN), .out(multiplexer_23_out), .sel(WEN));
  Multiplexer multiplexer_24 (.in0(1'b1), .in1(decoder_1_out11), .out(multiplexer_24_out), .sel(WEN));
  Multiplexer #(.width(8)) multiplexer_25 (.in0(I12), .in1(PORT_IN), .out(multiplexer_25_out), .sel(WEN));
  Multiplexer multiplexer_26 (.in0(1'b1), .in1(decoder_1_out12), .out(multiplexer_26_out), .sel(WEN));
  Multiplexer #(.width(8)) multiplexer_27 (.in0(I13), .in1(PORT_IN), .out(multiplexer_27_out), .sel(WEN));
  Multiplexer multiplexer_28 (.in0(1'b1), .in1(decoder_1_out13), .out(multiplexer_28_out), .sel(WEN));
  Multiplexer #(.width(8)) multiplexer_29 (.in0(I14), .in1(PORT_IN), .out(multiplexer_29_out), .sel(WEN));
  Multiplexer multiplexer_30 (.in0(1'b1), .in1(decoder_1_out14), .out(multiplexer_30_out), .sel(WEN));
  Multiplexer #(.width(8)) multiplexer_31 (.in0(I15), .in1(PORT_IN), .out(multiplexer_31_out), .sel(WEN));
  Multiplexer multiplexer_32 (.in0(1'b1), .in1(decoder_1_out15), .out(multiplexer_32_out), .sel(WEN));
  Register register_1 (.D(multiplexer_1_out), .en(multiplexer_2_out), .clk(CLK), .Q(O0), .clr(RST));
  Register register_2 (.D(multiplexer_3_out), .en(multiplexer_4_out), .clk(CLK), .Q(O1), .clr(RST));
  Register register_3 (.D(multiplexer_5_out), .en(multiplexer_6_out), .clk(CLK), .Q(O2), .clr(RST));
  Register register_4 (.D(multiplexer_7_out), .en(multiplexer_8_out), .clk(CLK), .Q(O3), .clr(RST));
  Register register_5 (.D(multiplexer_9_out), .en(multiplexer_10_out), .clk(CLK), .Q(O4), .clr(RST));
  Register register_6 (.D(multiplexer_11_out), .en(multiplexer_12_out), .clk(CLK), .Q(O5), .clr(RST));
  Register register_7 (.D(multiplexer_13_out), .en(multiplexer_14_out), .clk(CLK), .Q(O6), .clr(RST));
  Register register_8 (.D(multiplexer_15_out), .en(multiplexer_16_out), .clk(CLK), .Q(O7), .clr(RST));
  Register register_9 (.D(multiplexer_17_out), .en(multiplexer_18_out), .clk(CLK), .Q(O8), .clr(RST));
  Register register_10 (.D(multiplexer_19_out), .en(multiplexer_20_out), .clk(CLK), .Q(O9), .clr(RST));
  Register register_11 (.D(multiplexer_21_out), .en(multiplexer_22_out), .clk(CLK), .Q(O10), .clr(RST));
  Register register_12 (.D(multiplexer_23_out), .en(multiplexer_24_out), .clk(CLK), .Q(O11), .clr(RST));
  Register register_13 (.D(multiplexer_25_out), .en(multiplexer_26_out), .clk(CLK), .Q(O12), .clr(RST));
  Register register_14 (.D(multiplexer_27_out), .en(multiplexer_28_out), .clk(CLK), .Q(O13), .clr(RST));
  Register register_15 (.D(multiplexer_29_out), .en(multiplexer_30_out), .clk(CLK), .Q(O14), .clr(RST));
  Register register_16 (.D(multiplexer_31_out), .en(multiplexer_32_out), .clk(CLK), .Q(O15), .clr(RST));
  Pull_Resistor pull_resistor_1 (.node(PORT_OUT));
  assign PORT_OUT = PORT_EN ? multiplexer_33_out : 8'bz;  // Controlled_Buffer controlled_buffer_1
  Multiplexer #(.select(4), .width(8)) multiplexer_33 (
    .in0(O0), .in1(O1), .in2(O2), .in3(O3), .in4(O4), .in5(O5), .in6(O6), .in7(O7), .in8(O8), .in9(O9),
    .in10(O10), .in11(O11), .in12(O12), .in13(O13), .in14(O14), .in15(O15), .out(multiplexer_33_out),
    .sel(PORT_ADDR));
endmodule

module NUM_DSP (
  input  [7:0] NUM_IN,
  input  [7:0] DSP_SIGN,
  output [7:0] NUM_OUT,
  output [7:0] DSP_OUT
);

  wire adder_1_cout, adder_2_cout, adder_3_cout, adder_4_cout, adder_5_cout, adder_6_cout, adder_7_cout,
       and_1_out, xor_1_out, xor_2_out, xor_3_out, xor_4_out, xor_5_out, xor_6_out, xor_7_out, xor_8_out;
  wire [7:0] adder_1_out, pull_resistor_1_node;

  and and_1 (and_1_out, NUM_IN[7], DSP_SIGN[1]);
  xor xor_1 (xor_1_out, NUM_IN[0], and_1_out);
  xor xor_2 (xor_2_out, NUM_IN[1], and_1_out);
  xor xor_3 (xor_3_out, NUM_IN[2], and_1_out);
  xor xor_4 (xor_4_out, NUM_IN[3], and_1_out);
  xor xor_5 (xor_5_out, NUM_IN[4], and_1_out);
  xor xor_6 (xor_6_out, NUM_IN[5], and_1_out);
  xor xor_7 (xor_7_out, NUM_IN[6], and_1_out);
  xor xor_8 (xor_8_out, NUM_IN[7], and_1_out);
  Adder #(.width(1)) adder_1 (.a(xor_1_out), .b(1'b0), .out(adder_1_out[0]), .cin(and_1_out), .cout(adder_1_cout));
  Adder #(.width(1)) adder_2 (.a(xor_2_out), .b(1'b0), .out(adder_1_out[1]), .cin(adder_1_cout), .cout(adder_2_cout));
  Adder #(.width(1)) adder_3 (.a(xor_3_out), .b(1'b0), .out(adder_1_out[2]), .cin(adder_2_cout), .cout(adder_3_cout));
  Adder #(.width(1)) adder_4 (.a(xor_4_out), .b(1'b0), .out(adder_1_out[3]), .cin(adder_3_cout), .cout(adder_4_cout));
  Adder #(.width(1)) adder_5 (.a(xor_5_out), .b(1'b0), .out(adder_1_out[4]), .cin(adder_4_cout), .cout(adder_5_cout));
  Adder #(.width(1)) adder_6 (.a(xor_6_out), .b(1'b0), .out(adder_1_out[5]), .cin(adder_5_cout), .cout(adder_6_cout));
  Adder #(.width(1)) adder_7 (.a(xor_7_out), .b(1'b0), .out(adder_1_out[6]), .cin(adder_6_cout), .cout(adder_7_cout));
  Adder #(.width(1)) adder_8 (.a(xor_8_out), .b(1'b0), .out(adder_1_out[7]), .cin(adder_7_cout));  // open: cout
  LED SIGN (.in(DSP_SIGN[1]));
  LED SHOW (.in(DSP_SIGN[0]));
  _7_Segment_Display u_7_segment_display_1 (.g(and_1_out));  // open: f, a, b, e, d, c, dp
  _7_Segment_Display u_7_segment_display_2 ();  // open: g, f, a, b, e, d, c, dp
  // BCD_to_7_Segment_decoder bcd_to_7_segment_decoder_1: pin names not known
  Pull_Resistor pull_resistor_1 (.node(pull_resistor_1_node));
  assign pull_resistor_1_node = DSP_SIGN[0] ? adder_1_out : 8'bz;  // Controlled_Buffer controlled_buffer_1
  // Binary_to_BCD_converter #(.binvalue(8)) binary_to_bcd_converter_1: pin names not known; wires that end beside it: pull_resistor_1_node
  _7_Segment_Display u_7_segment_display_3 ();  // open: g, f, a, b, e, d, c, dp
  // BCD_to_7_Segment_decoder bcd_to_7_segment_decoder_2: pin names not known
  _7_Segment_Display u_7_segment_display_4 ();  // open: g, f, a, b, e, d, c, dp
  // BCD_to_7_Segment_decoder bcd_to_7_segment_decoder_3: pin names not known

  assign DSP_OUT = DSP_SIGN;
  assign NUM_OUT = NUM_IN;
endmodule
